# Fritzing sketch setup (saved by Fritzing 0.9.5d)
breadboards: 1

parts:
  Composant1 = Arduino Nano (Rev3.0)
  125_kHz_RFID_module1 = RDM6300
  LED1 = smd LED [color="Green (555nm)" package="1206 [SMD]"]
  R1 = Resistor [tolerance=±5% resistance=220 package="2512 [SMD]"]
  SG1 = Buzzer 12mm [package=buzzer-12mm-ns]
  L1 = Inductor [package="0603 [SMD]"]

nets:
  N1: Composant1.GND, 125_kHz_RFID_module1.GND#60, LED1.anode, SG1.1
  N2: Composant1.D2, SG1.2
  N3: Composant1.D3, R1.Pin_0
  N4: Composant1.D4, 125_kHz_RFID_module1.TX, 125_kHz_RFID_module1.GND#66
  N5: Composant1.5V, 125_kHz_RFID_module1.+5V#61
  N6: 125_kHz_RFID_module1.ANT1, L1.pin_0
  N7: 125_kHz_RFID_module1.ANT2, L1.pin_1
  N8: LED1.cathode, R1.Pin_1

notes:
  Antenna

custom parts:
  RDM6300: 125 kHz RFID module (serial interface)
